# Fritzing sketch Controlboard (saved by Fritzing 1.0.1rc)
circuit board: 5.03413cm x 5.45397cm
breadboards: 1

parts:
  VCC_GND = Screw terminal - 2 pins [package=THT]
  SDA_SCL = Screw terminal - 2 pins [package=THT]
  GND_VCC = Screw terminal - 2 pins [package=THT]
  SCL_SDA = Screw terminal - 2 pins [package=THT]
  VCC_GND_2 = Screw terminal - 2 pins [package=THT]
  SDA_SCL_2 = Screw terminal - 2 pins [package=THT]
  VCC_GND_3 = Screw terminal - 2 pins [package=THT]
  SDA_SCL_3 = Screw terminal - 2 pins [package=THT]
  C1 = Ceramic Capacitor [capacitance=100nF voltage=35V package="200 mil [THT, multilayer]"]
  C2 = Ceramic Capacitor [capacitance=100nF voltage=35V package="200 mil [THT, multilayer]"]
  C3 = Ceramic Capacitor [capacitance=100nF voltage=35V package="200 mil [THT, multilayer]"]
  C4 = Ceramic Capacitor [capacitance=100nF voltage=35V package="200 mil [THT, multilayer]"]

nets:
  N1: VCC_GND.pin1, GND_VCC.pin2, VCC_GND_3.pin2, C1.1, C2.1, C3.1
  N2: VCC_GND.pin2, VCC_GND_3.pin1, C1.0, C3.0
  N3: SDA_SCL.pin1, SCL_SDA.pin2, SDA_SCL_2.pin1, SDA_SCL_3.pin1
  N4: SDA_SCL.pin2, SCL_SDA.pin1, SDA_SCL_2.pin2, SDA_SCL_3.pin2
  N5: GND_VCC.pin1, VCC_GND_2.pin1, VCC_GND_2.pin2, C2.0, C4.0, C4.1
