# Fritzing sketch Mainboard (saved by Fritzing 0.9.6b)
circuit board: 4.8cm x 8.6cm
breadboards: 1

parts:
  Speaker = Piezo Speaker
  INT_SDA = Pad [width=7.902222222222222 height=9.03111111111111 connect=center]
  INT_SCL = Pad [width=7.902222222222222 height=9.03111111111111 connect=center]
  SB_SCL = Pad [width=7.902222222222222 height=9.03111111111111 connect=center]
  SB_SDA = Pad [width=7.902222222222222 height=9.03111111111111 connect=center]
  PICO_SOCKET_HERE = ZIFSOCKET-40-6 [package=dil40-6-zif_socket]
  SB_ID = Pad [width=7.902222222222222 height=9.03111111111111 connect=center]
  FLYWHEEL = Pad [width=7.902222222222222 height=9.03111111111111 connect=center]
  UART_TX = Pad [width=7.902222222222222 height=9.03111111111111 connect=center]
  UART_RX = Pad [width=7.902222222222222 height=9.03111111111111 connect=center]
  3_3v_IN = Pad [width=7.902222222222222 height=9.03111111111111 connect=center]
  GND_OUT = Pad [width=7.902222222222222 height=9.03111111111111 connect=center]
  C1 = Capacitor [package=cap-pth-small]
  R1 = Resistor [tolerance=±5% power=0.25 resistance=220 package=THT]
  C2 = Ceramic Capacitor [capacitance=100nF voltage=35V package="100 mil [THT, multilayer]"]
  Trigger = Pushbutton [package=THT]
  Safety = Pushbutton [package=THT]
  Rev_Pin = Pushbutton [package=THT]

nets:
  N1: Speaker.pin1, PICO_SOCKET_HERE.P$3, PICO_SOCKET_HERE.P$8, PICO_SOCKET_HERE.P$13, PICO_SOCKET_HERE.P$18, PICO_SOCKET_HERE.P$23, PICO_SOCKET_HERE.P$28, PICO_SOCKET_HERE.P$33, PICO_SOCKET_HERE.P$38, GND_OUT.pad, C1.2, C2.0
  N2: Speaker.pin2, PICO_SOCKET_HERE.P$20
  N3: INT_SDA.pad, PICO_SOCKET_HERE.P$24
  N4: INT_SCL.pad, PICO_SOCKET_HERE.P$25
  N5: SB_SCL.pad, PICO_SOCKET_HERE.P$27
  N6: SB_SDA.pad, PICO_SOCKET_HERE.P$26
  N7: PICO_SOCKET_HERE.P$12, FLYWHEEL.pad
  N8: PICO_SOCKET_HERE.P$17, Safety.leg0
  N9: PICO_SOCKET_HERE.P$19, Rev_Pin.leg0
  N10: PICO_SOCKET_HERE.P$21, UART_TX.pad
  N11: PICO_SOCKET_HERE.P$22, UART_RX.pad
  N12: PICO_SOCKET_HERE.P$31, PICO_SOCKET_HERE.P$36, R1.Pin_1
  N13: PICO_SOCKET_HERE.P$32, SB_ID.pad, R1.Pin_0
  N14: PICO_SOCKET_HERE.P$34, Trigger.leg0
  N15: PICO_SOCKET_HERE.P$39, 3_3v_IN.pad, C1.1, C2.1, Trigger.leg1, Safety.leg1, Rev_Pin.leg1

notes:
  Rev. 0.0.8
