# Fritzing sketch Motor Controlboard (saved by Fritzing 1.0.1rc)
circuit board: 6.59411cm x 17.7748cm
breadboards: 1

parts:
  MTR_1_OUT = Screw terminal - 2 pins [package=THT]
  NPN = Basic FET N-Channel-flat [package="TO220 [THT]"]
  PNP = Basic FET N-Channel-flat [package="TO220 [THT]"]
  NPN_2 = Basic FET N-Channel-flat [package="TO220 [THT]"]
  PNP_2 = Basic FET N-Channel-flat [package="TO220 [THT]"]
  Q2 = NPN-Transistor [package="TO92 [THT]"]
  Q1 = NPN-Transistor [package="TO92 [THT]"]
  D1 = Diode [package=diode-1n4148]
  D2 = Diode [package=diode-1n4148]
  D3 = Diode [package=diode-1n4148]
  D4 = Diode [package=diode-1n4148]
  NPN1 = Basic FET N-Channel-flat [package="TO220 [THT]"]
  D5 = Diode [package=diode-1n4148]
  MTR_2_OUT = Screw terminal - 2 pins [package=THT]
  NPN2 = Basic FET N-Channel-flat [package="TO220 [THT]"]
  NPN3 = Basic FET N-Channel-flat [package="TO220 [THT]"]
  NPN4 = Basic FET N-Channel-flat [package="TO220 [THT]"]
  PNP1 = Basic FET N-Channel-flat [package="TO220 [THT]"]
  PNP2 = Basic FET N-Channel-flat [package="TO220 [THT]"]
  Q3 = NPN-Transistor [package="TO92 [THT]"]
  Q4 = NPN-Transistor [package="TO92 [THT]"]
  D6 = Diode [package=diode-1n4148]
  D7 = Diode [package=diode-1n4148]
  D8 = Diode [package=diode-1n4148]
  D9 = Diode [package=diode-1n4148]
  D10 = Diode [package=diode-1n4148]
  FWD_REV_PWM = screw terminal, 3 pins
  FWD_REV_PWM_2 = screw terminal, 3 pins
  VCC_GND = Screw terminal - 2 pins [package=THT]
  SOL_IN_GND = Screw terminal - 2 pins [package=THT]
  NPN5 = Basic FET N-Channel-flat [package="TO220 [THT]"]
  D11 = Diode [package=diode-1n4148]
  SOL_OUT = Screw terminal - 2 pins [package=THT]

nets:
  N1: MTR_1_OUT.pin1, Q2.C, Q1.C, MTR_2_OUT.pin1, Q3.C, Q4.C, VCC_GND.pin1, SOL_IN_GND.pin1, SOL_OUT.pin1
  N2: MTR_1_OUT.pin2, NPN.2, PNP.2, NPN_2.2, PNP_2.2, D1.A, D2.A, D3.A, D4.A
  N3: NPN.1, NPN_2.1, FWD_REV_PWM.pin2
  N4: NPN.3, PNP.3, NPN_2.3, PNP_2.3, D1.C, D2.C, D3.C, D4.C, NPN1.2, D5.A
  N5: PNP.1, Q1.E
  N6: PNP_2.1, Q2.E
  N7: Q2.B, Q1.B, FWD_REV_PWM.pin3
  N8: NPN1.1, FWD_REV_PWM.pin1
  N9: NPN1.3, D5.C, NPN3.3, D10.C, VCC_GND.pin2
  N10: MTR_2_OUT.pin2, NPN2.2, NPN4.2, PNP1.2, PNP2.2, D6.A, D7.A, D8.A, D9.A
  N11: NPN2.1, NPN4.1, FWD_REV_PWM_2.pin2
  N12: NPN2.3, NPN3.2, NPN4.3, PNP1.3, PNP2.3, D6.C, D7.C, D8.C, D9.C, D10.A
  N13: NPN3.1, FWD_REV_PWM_2.pin1
  N14: PNP1.1, Q4.E
  N15: PNP2.1, Q3.E
  N16: Q3.B, Q4.B, FWD_REV_PWM_2.pin3
  N17: SOL_IN_GND.pin2, NPN5.1
  N18: NPN5.2, D11.A, SOL_OUT.pin2
  N19: NPN5.3, D11.C

notes:
  MOTOR ONE
  MOTOR TWO
  SOLENOID

custom parts:
  Basic FET N-Channel-flat: MOSFET N-Channel Transistor lying flat on PCB. 16.7mm from mounting hole centre to leg hole centres.
